# Fritzing sketch TrafficLight (saved by Fritzing 0.9.3b)
circuit board: 6.88566cm x 5.36311cm
breadboards: 1

parts:
  LED1 = LED - 5mm [color="Red (633nm)" package="5 mm [THT]"]
  LED2 = LED - 5mm [color="Yellow (592nm)" package="5 mm [THT]"]
  LED3 = LED - 5mm [color="Green (555nm)" package="5 mm [THT]"]
  R1 = Resistor [tolerance=±5% resistance=220 package=THT]
  R2 = Resistor [tolerance=±5% resistance=220 package=THT]
  R3 = Resistor [tolerance=±5% resistance=220 package=THT]
  Arduino1 = Arduino Uno (Rev3)
  S1 = Pushbutton [package=THT]
  R6 = Resistor [tolerance=±5% resistance=100k package=THT]

nets (from the pcb view):
  N1: LED1.cathode, R1.Pin_0
  N2: LED1.anode, Arduino1.D12/MISO
  N3: LED2.cathode, R2.Pin_0
  N4: LED2.anode, Arduino1.D11_PWM/MOSI
  N5: LED3.cathode, R3.Pin_0
  N6: LED3.anode, Arduino1.D10_PWM/SS
  N7: R3.Pin_1, Arduino1.GND, R6.Pin_1
  N8: Arduino1.D2, S1.leg0, R6.Pin_0
  N9: Arduino1.5V, S1.leg1
